# Fritzing sketch schematic (saved by Fritzing 0.9.3b)
breadboards: 1

parts:
  Εξάρτημα1 = Arduino Uno (Rev3)
  U1 = LCD-16X2 [package=lcd-16x2]
  RHT1 = Humidity and Temperature Sensor RHT03
  U2 = POT [package=pot_mammoth]
  U3 = ESP8266 WiFi Module [part_number=ESP8266]
  Εξάρτημα2 = HC-SR501 Body Sensor Module
  Εξάρτημα3 = MQ-9 breakout
  R1 = Resistor [tolerance=±5% resistance=220 package=THT]
  R2 = Resistor [tolerance=±5% resistance=10k package=THT]
  R3 = Resistor [tolerance=±5% resistance=1k package=THT]
  R4 = Resistor [tolerance=±5% resistance=2k package=THT]

nets:
  N1: Εξάρτημα1.A0, Εξάρτημα3.AO
  N2: Εξάρτημα1.D8, R3.Pin_0
  N3: Εξάρτημα1.D9_PWM, RHT1.Data-signal
  N4: Εξάρτημα1.D11_PWM/MOSI, U1.E
  N5: Εξάρτημα1.D12/MISO, U1.RS
  N6: Εξάρτημα1.D2, U1.DB7
  N7: Εξάρτημα1.D3_PWM, U1.DB6
  N8: Εξάρτημα1.D4, U1.DB5
  N9: Εξάρτημα1.D5_PWM, U1.DB4
  N10: Εξάρτημα1.D6_PWM, Εξάρτημα2.OUT
  N11: Εξάρτημα1.D7, U3.TXD
  3V3: Εξάρτημα1.3V3, U3.VCC
  VCC: Εξάρτημα1.5V, U1.VDD, RHT1.Vcc, U2.E, Εξάρτημα2.VCC, Εξάρτημα3.VCC, R1.Pin_1
  GND: Εξάρτημα1.GND, U1.VSS, U1.R_W, U1.K, RHT1.GND_2, U2.S, U3.GND, Εξάρτημα2.GND, Εξάρτημα3.GND
  N12: U1.VO, U2.A
  N13: U1.A, R1.Pin_0
  N14: U3.RXD, R3.Pin_1, R4.Pin_0
  N15: U3.CH_PD, R2.Pin_0

custom parts:
  ESP8266 WiFi Module: Generic WiFi Module based on the ESP8266 with onboard PCB antenna and UART communications
  HC-SR501 Body Sensor Module: Pyroelectric Infrared PIR Motion Sensor Detector Module
  MQ-9 breakout: SKU: 101284
